// Logisim project 4-Bit-ALU Group 5.circ as structural Verilog: 3 circuits, main circuit main
module main (
  input  s2,
  input  s1,
  input  s0,
  input  A,
  input  B,
  output out_6,
  output out_7
);

  wire and_1_out, and_2_out, and_3_out, and_4_out, not_1_out, not_2_out, or_1_out, or_2_out;

  not not_1 (not_1_out, s0);
  not not_2 (not_2_out, s1);
  and and_1 (and_1_out, s1, s0);
  and and_2 (and_2_out, s2, not_1_out);
  and and_3 (and_3_out, B, not_2_out, s0);
  and and_4 (and_4_out, B, not_2_out, not_1_out);
  or or_1 (or_1_out, A, and_3_out);
  or or_2 (or_2_out, and_1_out, and_4_out);
  Adder #(.width(1)) adder_1 (.a(or_1_out), .b(or_2_out), .out(out_6), .cin(and_2_out), .cout(out_7));
endmodule

module myalu (
  input  [3:0] B,
  input  [3:0] A,
  input  [2:0] Select,
  output [3:0] F,
  output Z,
  output S,
  output V,
  output C
);

  wire and_1_out, main_1_out_7, main_2_out_7, main_3_out_7, main_4_out_7, not_1_out;

  not not_1 (not_1_out, Select[0]);
  main main_1 (.s2(Select[2]), .s1(Select[1]), .s0(Select[0]), .A(A[0]), .B(B[0]), .out_6(F[0]), .out_7(main_1_out_7));
  main main_2 (
    .s2(main_1_out_7), .s1(Select[1]), .s0(Select[0]), .A(A[1]), .B(B[1]), .out_6(F[1]), .out_7(main_2_out_7));
  main main_3 (
    .s2(main_2_out_7), .s1(Select[1]), .s0(Select[0]), .A(A[2]), .B(B[2]), .out_6(F[2]), .out_7(main_3_out_7));
  main main_4 (
    .s2(main_3_out_7), .s1(Select[1]), .s0(Select[0]), .A(A[3]), .B(B[3]), .out_6(F[3]), .out_7(main_4_out_7));
  and and_1 (and_1_out, main_3_out_7, not_1_out);
  and and_2 (C, main_4_out_7, not_1_out);
  nor nor_1 (Z, F[3], F[2], F[1], F[0]);
  xor xor_1 (V, and_1_out, C);

  assign S = F[3];
endmodule

module Final_alu (
  input  [3:0] A,
  input  [3:0] B,
  input  [2:0] Select,
  output C,
  output V,
  output S,
  output Z,
  output [3:0] Output
);

  myalu myalu_1 (.A(A), .B(B), .F(Output), .V(V), .S(S), .C(C), .Z(Z), .Select(Select));
endmodule
