// Logisim project Edited by naeem.circ as structural Verilog: 6 circuits, main circuit main
module main (
  input  [15:0] A,
  input  [15:0] B,
  output [3:0] out_3,
  output [13:0] Larger,
  output [13:0] Smaller,
  output [3:0] out_6,
  output [13:0] out_7,
  output [13:0] out_8,
  output [4:0] out_9,
  output [3:0] out_10,
  output [10:0] out_11,
  output [4:0] out_12,
  output [15:0] Output,
  output Overflow
);

  wire Compare_Exp_x__y, Compare_Exp_x_y;
  wire [13:0] Adjust_SignBit_2_out_3, Adjust_SignBit_out_3, Complementing_result_output;

  Compare Compare_Exp (
    .X(A[14:11]), .Y(B[14:11]), .X__Y(Compare_Exp_x__y), .X_Y(Compare_Exp_x_y), .Difference(out_3),
    .Larger(out_6));  // open: out_6
  Adjust_Sign Adjust_SignBit (.in_1({3'b001, A[10:0]}), .Sign_Bit(A[15]), .out_3(Adjust_SignBit_out_3));
  Adder #(.width(5)) adder_1 (.a(5'b00010), .b({1'b0, out_6}), .out(out_9), .cin(1'b0));  // open: cout
  Multiplexer #(.width(14), .disabled(0), .enable("false")) multiplexer_1 (
    .in0(Adjust_SignBit_out_3), .in1(Adjust_SignBit_2_out_3), .out(Smaller), .sel(Compare_Exp_x__y));
  Shifter #(.width(14), .shift("ar")) shifter_1 (.in(Smaller), .\dist (out_3), .out(out_7));
  Subtractor #(.width(5)) subtractor_1 (.a(out_9), .b({1'b0, out_10}), .out(out_12), .bin(1'b0));  // open: bout
  Multiplexer #(.width(14), .disabled(0), .enable("false")) multiplexer_2 (
    .in0(Adjust_SignBit_out_3), .in1(Adjust_SignBit_2_out_3), .out(Larger), .sel(Compare_Exp_x_y));
  Adjust_Sign Adjust_SignBit_2 (.in_1({3'b001, B[10:0]}), .Sign_Bit(B[15]), .out_3(Adjust_SignBit_2_out_3));
  Adder #(.width(14)) adder_2 (.a(Larger), .b(out_7), .out(out_8), .cin(1'b0));  // open: cout
  Normalize Normalize (.Input(Complementing_result_output), .Shift_Amount(out_10), .Truncated_Fraction(out_11));
  Complementing_result Complementing_result (.Input(out_8), .Output(Complementing_result_output), .Sign(Output[15]));

  assign Output[14:0] = {out_12[3:0], out_11};
  assign Overflow = out_12[4];
endmodule

module Compare (
  input  [3:0] X,
  input  [3:0] Y,
  output X__Y,
  output X_Y,
  output [3:0] Difference,
  output out_6,
  output [3:0] Larger
);

  wire comparator_1_eq, comparator_1_gt;
  wire [3:0] multiplexer_1_out;

  Comparator #(.width(4), .mode("unsigned")) comparator_1 (
    .a(X), .b(Y), .gt(comparator_1_gt), .eq(comparator_1_eq), .lt(X_Y));
  or or_1 (X__Y, comparator_1_gt, comparator_1_eq);
  Multiplexer #(.width(4), .disabled(0), .enable("false")) multiplexer_1 (
    .in0(X), .in1(Y), .out(multiplexer_1_out), .sel(X__Y));
  Multiplexer #(.width(4), .disabled(0), .enable("false")) multiplexer_2 (.in0(X), .in1(Y), .out(Larger), .sel(X_Y));
  Subtractor #(.width(4)) subtractor_1 (.a(Larger), .b(multiplexer_1_out), .out(Difference), .bin(1'b0), .bout(out_6));

  // Notes on the sheet:
  //   X>=Y
  //   smaller
  //   larger
  //   larger - smaller
endmodule

module Add (
  input  [12:0] in_1,
  input  [12:0] in_2
);
endmodule

module Adjust_Sign (
  input  [13:0] in_1,
  input  Sign_Bit,
  output [13:0] out_3
);

  wire [13:0] negator_1_out;

  Negator #(.width(14)) negator_1 (.in(in_1), .out(negator_1_out));
  Multiplexer #(.width(14), .disabled(0), .enable("false")) multiplexer_1 (
    .in0(in_1), .in1(negator_1_out), .out(out_3), .sel(Sign_Bit));
endmodule

module Normalize (
  input  [13:0] Input,
  output [3:0] Shift_Amount,
  output [10:0] Truncated_Fraction
);

  wire [13:0] shifter_1_out;

  BitFinder #(.width(14)) bitfinder_1 (
    .in({Input[0], Input[1], Input[2], Input[3], Input[4], Input[5], Input[6], Input[7], Input[8], Input[9], Input[10], Input[11], Input[12], 1'b0}),
    .index(Shift_Amount));  // open: found
  Shifter #(.width(14)) shifter_1 (
    .in(Input), .\dist (Shift_Amount), .out({shifter_1_out[13], Truncated_Fraction, shifter_1_out[1:0]}));
endmodule

module Complementing_result (
  input  [13:0] Input,
  output [13:0] Output,
  output Sign
);

  wire [13:0] negator_1_out;

  Negator #(.width(14)) negator_1 (.in(Input), .out(negator_1_out));
  Multiplexer #(.width(14), .disabled(0), .enable("false")) multiplexer_1 (
    .in0(Input), .in1(negator_1_out), .out(Output), .sel(Input[13]));

  assign Sign = Input[13];
endmodule
