// Logisim project NormalizeNow.circ as structural Verilog: 2 circuits, main circuit Normalizer
module BitFinder (
  input  [12:0] Input,
  output [3:0] Shift
);

  wire [3:0] bitfinder_1_index;

  BitFinder_part #(.width(13)) bitfinder_1 (
    .in({Input[0], Input[1], Input[2], Input[3], Input[4], Input[5], Input[6], Input[7], Input[8], Input[9], Input[10], Input[11], Input[12]}),
    .index(bitfinder_1_index));  // open: found
  Subtractor #(.width(4)) subtractor_1 (.a(bitfinder_1_index), .b(4'b0000), .out(Shift), .bin(1'b1));  // open: bout
endmodule

module Normalizer (
  input  [3:0] LargeExpo,
  input  [12:0] Fraction,
  output [3:0] FinalExpo,
  output [12:0] FinalFraction,
  output [3:0] ShiftNeeded
);

  Subtractor #(.width(4)) subtractor_1 (.a(LargeExpo), .b(ShiftNeeded), .out(FinalExpo));  // open: bin, bout
  BitFinder bitfinder_1 (.Input(Fraction), .Shift(ShiftNeeded));
  Shifter #(.width(13)) shifter_1 (.in(Fraction), .\dist (ShiftNeeded), .out(FinalFraction));
endmodule
