// Logisim project NormalizeNow2.circ as structural Verilog: 2 circuits, main circuit Normalizer
module BitFinder (
  input  [13:0] Input,
  output [3:0] Shift
);

  BitFinder_part #(.width(14)) bitfinder_1 (
    .in({Input[0], Input[1], Input[2], Input[3], Input[4], Input[5], Input[6], Input[7], Input[8], Input[9], Input[10], Input[11], Input[12], 1'b0}),
    .index(Shift));  // open: found
endmodule

module Normalizer (
  input  [3:0] LargeExpo,
  input  [12:0] Fraction,
  output [3:0] FinalExpo,
  output [12:0] FinalFraction,
  output [3:0] ShiftNeeded
);

  wire [13:13] undriven;

  Subtractor #(.width(4)) subtractor_1 (.a(LargeExpo), .b(ShiftNeeded), .out(FinalExpo));  // open: bin, bout
  BitFinder bitfinder_1 (.Input({undriven[13], Fraction}), .Shift(ShiftNeeded));
  Shifter #(.width(13)) shifter_1 (.in(Fraction), .\dist (ShiftNeeded), .out(FinalFraction));
  // Pins of 13 and 14 bits meet at {undriven[13], Fraction}
endmodule
