// Logisim project Control_ALU-with label_2.circ as structural Verilog: 3 circuits, main circuit main
module main (
  input  [7:0] in_1,
  input  [7:0] in_2,
  input  [3:0] in_3,
  output out_4,
  output [7:0] out_5
);

  wire [2:0] Control_aluop;

  control_unit Control (
    .OpCode(in_3), .ALUOp(Control_aluop));  // open: ALUSrc, Bneq, Beq, MemToReg, MemWrite, MemRead, RegWrite, RegDst, Shift
  ALU ALU (.A(in_1), .B(in_2), .ALUop(Control_aluop), .ZF(out_4), .F(out_5));  // open: overflow, negative
endmodule

module ALU (
  input  [7:0] A,
  input  [7:0] B,
  input  [2:0] ALUop,
  output overflow,
  output ZF,
  output negative,
  output [7:0] F
);

  wire [7:0] adder_1_out, and_1_out, nor_1_out, or_1_out, subtractor_1_out;
  wire [15:0] shifter_1_out, shifter_2_out;

  Adder adder_1 (.a(A), .b(B), .out(adder_1_out), .cin(1'b0), .cout(overflow));
  Subtractor subtractor_1 (.a(A), .b(B), .out(subtractor_1_out), .bin(1'b0), .bout(negative));
  assign or_1_out = A | B;  // OR_Gate or_1, 8 bits wide
  assign and_1_out = A & B;  // AND_Gate and_1, 8 bits wide
  assign nor_1_out = ~(A | B);  // NOR_Gate nor_1, 8 bits wide
  Shifter #(.width(16)) shifter_1 (.in({{8{1'b0}}, A}), .\dist (B[3:0]), .out(shifter_1_out));
  Shifter #(.width(16), .shift("lr")) shifter_2 (.in({{8{1'b0}}, A}), .\dist (B[3:0]), .out(shifter_2_out));
  Multiplexer #(.select(3), .width(8), .enable("false")) multiplexer_1 (
    .in0(adder_1_out), .in1(subtractor_1_out), .in2(or_1_out), .in3(and_1_out), .in4(nor_1_out),
    .in5(shifter_1_out[7:0]), .in6(shifter_2_out[7:0]), .in7({8{1'b0}}), .out(F), .sel(ALUop));
  nor nor_2 (ZF, F[0], F[1], F[2], F[3], F[4], F[5], F[6], F[7]);
endmodule

module control_unit (
  input  [3:0] OpCode,
  output [2:0] ALUOp,
  output ALUSrc,
  output Bneq,
  output Beq,
  output MemToReg,
  output MemWrite,
  output MemRead,
  output RegWrite,
  output RegDst,
  output Shift
);

  ROM #(.addrWidth(4), .dataWidth(12)) rom_1 (
    .addr(OpCode), .data({Shift, RegDst, RegWrite, MemRead, MemWrite, MemToReg, Beq, Bneq, ALUSrc, ALUOp}));  // open: sel

  // Notes on the sheet:
  //   contents of rom_1 (hex, n*v repeats v):
  //   88 21 604 e0d 20b 20a 0 208 603 601 11 602 e0e 348 600 209
endmodule
