// Logisim project test123.circ as structural Verilog: 1 circuit, main circuit main
module main (
  input  [3:0] in_1,
  output [11:0] out_2
);

  ROM #(.addrWidth(4), .dataWidth(12)) rom_1 (.addr(in_1), .data(out_2));  // open: sel

  // Notes on the sheet:
  //   contents of rom_1 (hex, n*v repeats v):
  //   123 0 432
endmodule
