// Logisim project A1_Group5 circuit.circ as structural Verilog: 12 circuits, main circuit main
module main (
  input  Clear_All,
  input  Manual_Input_enable,
  input  [7:0] Manual_Data_Input,
  input  [3:0] Manual_Data_Address,
  output [3:0] reg_rs,
  output [3:0] reg_rt,
  output [7:0] A,
  output [7:0] B,
  output [7:0] result,
  output [3:0] Opcode,
  output [7:0] PC,
  output [19:0] Instruction,
  output [3:0] rd,
  output [7:0] Write_Data,
  output [7:0] sp,
  output [7:0] t5,
  output [7:0] t4,
  output [7:0] zero,
  output [7:0] t0,
  output [7:0] t1,
  output [7:0] t2,
  output [7:0] t3
);

  wire CLK_Manual_out, CLK_out, control_reg_wrt, EX_MEM_REG_reg_wrt, id_ex_reg_1_reg_wrt_2,
       MEM_WB_REG_reg_wrt, multiplexer_1_out, or_1_out;
  wire [1:0] Forwarding_Unit_forward_a, Forwarding_Unit_forward_b;
  wire [2:0] control_aluop, id_ex_reg_1_aluop_2;
  wire [3:0] EX_MEM_REG_reg_rd_addrs_2, id_ex_reg_1_reg_rd_address_2, id_ex_reg_1_reg_rs_address_2,
       id_ex_reg_1_reg_rt_address_2, MEM_WB_REG_reg_rd_addrs_2;
  wire [7:0] adder_1_out, EX_MEM_REG_alu_reslt, id_ex_reg_1_reg_rs_data_2, id_ex_reg_1_reg_rt_data_2,
       IF_ID_REG_instruction_2, multiplexer_2_out, register_file_1_read_data_1, register_file_1_read_data_2;

  Clock CLK (.out(CLK_out));
  Clock CLK_Manual (.out(CLK_Manual_out));
  Register #(.trigger("falling")) register_1 (.D(adder_1_out), .Q(PC), .clk(CLK_out), .clr(Clear_All));  // open: en
  Adder adder_1 (.a(PC), .b(8'h1), .out(adder_1_out), .cin(1'b0));  // open: cout
  Multiplexer #(.enable("false")) multiplexer_1 (
    .in0(CLK_out), .in1(CLK_Manual_out), .out(multiplexer_1_out), .sel(Manual_Input_enable));
  ROM #(.dataWidth(20)) rom_1 (.addr(PC), .data(Instruction));  // open: sel
  Multiplexer #(.width(8), .enable("false")) multiplexer_2 (
    .in0(Write_Data), .in1(Manual_Data_Input), .out(multiplexer_2_out), .sel(Manual_Input_enable));
  Multiplexer #(.width(4), .enable("false")) multiplexer_3 (
    .in0(MEM_WB_REG_reg_rd_addrs_2), .in1(Manual_Data_Address), .out(rd), .sel(Manual_Input_enable));
  IF_ID_REG IF_ID_REG (
    .Instruction(Instruction), .clk(CLK_out), .clr(Clear_All),
    .Instruction_2({Opcode, reg_rs, reg_rt, IF_ID_REG_instruction_2}));
  control control (.OpCode(Opcode), .ALUOp(control_aluop), .REG_WRT(control_reg_wrt));
  or or_1 (or_1_out, Manual_Input_enable, MEM_WB_REG_reg_wrt);
  register_file register_file_1 (
    .Read_Register_1(reg_rs), .Read_Register_2(reg_rt), .Write_Register(rd), .Write_Data(multiplexer_2_out),
    .Write_Signal(or_1_out), .CLK(multiplexer_1_out), .Clear(Clear_All), .zero(zero), .t0(t0), .t1(t1),
    .t2(t2), .t3(t3), .t4(t4), .t5(t5), .sp(sp), .Read_Data_1(register_file_1_read_data_1),
    .Read_Data_2(register_file_1_read_data_2));
  ID_EX_REG id_ex_reg_1 (
    .reg_rs_data(register_file_1_read_data_1), .reg_rt_data(register_file_1_read_data_2),
    .reg_rd_address(IF_ID_REG_instruction_2[7:4]), .reg_rs_address(reg_rs), .reg_rt_address(reg_rt),
    .ALUOP(control_aluop), .REG_WRT(control_reg_wrt), .clear(Clear_All), .clk(CLK_out),
    .reg_rs_data_2(id_ex_reg_1_reg_rs_data_2), .reg_rt_data_2(id_ex_reg_1_reg_rt_data_2),
    .reg_rd_address_2(id_ex_reg_1_reg_rd_address_2), .reg_rs_address_2(id_ex_reg_1_reg_rs_address_2),
    .reg_rt_address_2(id_ex_reg_1_reg_rt_address_2), .ALUOP_2(id_ex_reg_1_aluop_2),
    .reg_wrt_2(id_ex_reg_1_reg_wrt_2));
  Multiplexer #(.select(2), .width(8)) multiplexer_4 (
    .in0(id_ex_reg_1_reg_rs_data_2), .in1(Write_Data), .in2(EX_MEM_REG_alu_reslt), .out(A),
    .sel(Forwarding_Unit_forward_a), .en(1'b1));  // open: in3
  Multiplexer #(.select(2), .width(8)) multiplexer_5 (
    .in0(id_ex_reg_1_reg_rt_data_2), .in1(Write_Data), .in2(EX_MEM_REG_alu_reslt), .out(B),
    .sel(Forwarding_Unit_forward_b), .en(1'b1));  // open: in3
  ALU alu_1 (.A(A), .B(B), .ALUop(id_ex_reg_1_aluop_2), .F(result));  // open: overflow, negative, ZF
  Forwarding_Unit Forwarding_Unit (
    .ID_EX_Reg_rt(id_ex_reg_1_reg_rt_address_2), .ID_EX_Reg_rs(id_ex_reg_1_reg_rs_address_2),
    .MEM_WB_Red_rd(MEM_WB_REG_reg_rd_addrs_2), .EX_MEM_Reg_rd(EX_MEM_REG_reg_rd_addrs_2),
    .FORWARD_A(Forwarding_Unit_forward_a), .FORWARD_B(Forwarding_Unit_forward_b));
  EX_MEM_REG EX_MEM_REG (
    .alu_result(result), .reg_rd_addrs(id_ex_reg_1_reg_rd_address_2), .in_3(id_ex_reg_1_reg_wrt_2),
    .clear(Clear_All), .clk(CLK_out), .alu_reslt(EX_MEM_REG_alu_reslt),
    .reg_rd_addrs_2(EX_MEM_REG_reg_rd_addrs_2), .reg_wrt(EX_MEM_REG_reg_wrt));
  MEM_WB_REG MEM_WB_REG (
    .alu_result(EX_MEM_REG_alu_reslt), .reg_rd_addrs(EX_MEM_REG_reg_rd_addrs_2), .in_3(EX_MEM_REG_reg_wrt),
    .clear(Clear_All), .clk(CLK_out), .alu_reslt(Write_Data), .reg_rd_addrs_2(MEM_WB_REG_reg_rd_addrs_2),
    .reg_wrt(MEM_WB_REG_reg_wrt));

  // Notes on the sheet:
  //   Clear CLK
  //   contents of rom_1 (hex, n*v repeats v):
  //   e3330 94340 83420
endmodule

// Register File
module register_file (
  input  [3:0] Read_Register_1,
  input  [3:0] Read_Register_2,
  input  [3:0] Write_Register,
  input  [7:0] Write_Data,
  input  Write_Signal,
  input  CLK,
  input  Clear,
  output [7:0] Read_Data_1,
  output [7:0] Read_Data_2,
  output [7:0] sp,
  output [7:0] zero,
  output [7:0] t5,
  output [7:0] t0,
  output [7:0] t4,
  output [7:0] t1,
  output [7:0] t2,
  output [7:0] t3
);

  wire and_1_out, and_2_out, and_3_out, and_4_out, and_5_out, and_6_out, and_7_out, and_8_out,
       decoder_1_out0, decoder_1_out1, decoder_1_out2, decoder_1_out3, decoder_1_out4, decoder_1_out5,
       decoder_1_out6, decoder_1_out7, multiplexer_1_out, multiplexer_3_out;
  wire [7:0] multiplexer_2_out;

  Decoder #(.select(4), .enable("false")) decoder_1 (
    .out0(decoder_1_out0), .out1(decoder_1_out1), .out2(decoder_1_out2), .out3(decoder_1_out3),
    .out4(decoder_1_out4), .out5(decoder_1_out5), .out6(decoder_1_out6), .out7(decoder_1_out7),
    .sel(Write_Register));  // open: out8, out9, out10, out11, out12, out13, out14, out15
  and and_1 (and_1_out, decoder_1_out0, 1'b0);
  and and_2 (and_2_out, decoder_1_out1, Write_Signal);
  and and_3 (and_3_out, decoder_1_out2, Write_Signal);
  and and_4 (and_4_out, decoder_1_out3, Write_Signal);
  and and_5 (and_5_out, decoder_1_out4, Write_Signal);
  and and_6 (and_6_out, decoder_1_out5, Write_Signal);
  and and_7 (and_7_out, decoder_1_out6, Write_Signal);
  and and_8 (and_8_out, decoder_1_out7, Write_Signal);
  Multiplexer #(.enable("false")) multiplexer_1 (.in0(and_8_out), .in1(Clear), .out(multiplexer_1_out), .sel(Clear));
  Multiplexer #(.width(8), .enable("false")) multiplexer_2 (
    .in0(Write_Data), .in1({8{1'b1}}), .out(multiplexer_2_out), .sel(Clear));
  Register u_zero (.D(Write_Data), .en(and_1_out), .Q(zero), .clk(CLK), .clr(Clear));
  Register u_t0 (.D(Write_Data), .en(and_2_out), .Q(t0), .clk(CLK), .clr(Clear));
  Register u_t1 (.D(Write_Data), .en(and_3_out), .Q(t1), .clk(CLK), .clr(Clear));
  Register u_t2 (.D(Write_Data), .en(and_4_out), .Q(t2), .clk(CLK), .clr(Clear));
  Register u_t3 (.D(Write_Data), .en(and_5_out), .Q(t3), .clk(CLK), .clr(Clear));
  Register u_t4 (.D(Write_Data), .en(and_6_out), .Q(t4), .clk(CLK), .clr(Clear));
  Register u_t5 (.D(Write_Data), .en(and_7_out), .Q(t5), .clk(CLK), .clr(Clear));
  Register u_sp (.D(multiplexer_2_out), .en(multiplexer_1_out), .Q(sp), .clk(multiplexer_3_out));  // open: clr
  Multiplexer #(.enable("false")) multiplexer_3 (.in0(CLK), .in1(Clear), .out(multiplexer_3_out), .sel(Clear));
  Multiplexer #(.select(4), .width(8), .enable("false")) multiplexer_4 (
    .in0(zero), .in1(t0), .in2(t1), .in3(t2), .in4(t3), .in5(t4), .in6(t5), .in7(sp), .out(Read_Data_1),
    .sel(Read_Register_1));  // open: in8, in9, in10, in11, in12, in13, in14, in15
  Multiplexer #(.select(4), .width(8), .enable("false")) multiplexer_5 (
    .in0(zero), .in1(t0), .in2(t1), .in3(t2), .in4(t3), .in5(t4), .in6(t5), .in7(sp), .out(Read_Data_2),
    .sel(Read_Register_2));  // open: in8, in9, in10, in11, in12, in13, in14, in15
endmodule

module instruction_memory (
  input  [3:0] PC,
  output [19:0] Instruction_0_19
);

  ROM #(.addrWidth(4), .dataWidth(20)) rom_1 (.addr(PC), .data(Instruction_0_19));  // open: sel

  // Notes on the sheet:
  //   contents of rom_1 (hex, n*v repeats v):
  //   0 ed d 1212 0 1 0 1 101
endmodule

module ALU (
  input  [7:0] A,
  input  [7:0] B,
  input  [2:0] ALUop,
  output overflow,
  output ZF,
  output negative,
  output [7:0] F
);

  wire [7:0] adder_1_out, and_1_out, nor_1_out, or_1_out, subtractor_1_out;
  wire [15:0] shifter_1_out, shifter_2_out;

  Adder adder_1 (.a(A), .b(B), .out(adder_1_out), .cin(1'b0), .cout(overflow));
  Subtractor subtractor_1 (.a(A), .b(B), .out(subtractor_1_out), .bin(1'b0), .bout(negative));
  assign or_1_out = A | B;  // OR_Gate or_1, 8 bits wide
  assign and_1_out = A & B;  // AND_Gate and_1, 8 bits wide
  assign nor_1_out = ~(A | B);  // NOR_Gate nor_1, 8 bits wide
  Shifter #(.width(16)) shifter_1 (.in({{8{1'b0}}, A}), .\dist (B[3:0]), .out(shifter_1_out));
  Shifter #(.width(16), .shift("lr")) shifter_2 (.in({{8{1'b0}}, A}), .\dist (B[3:0]), .out(shifter_2_out));
  Multiplexer #(.select(3), .width(8), .enable("false")) multiplexer_1 (
    .in0(adder_1_out), .in1(subtractor_1_out), .in2(or_1_out), .in3(and_1_out), .in4(nor_1_out),
    .in5(shifter_1_out[7:0]), .in6(shifter_2_out[7:0]), .in7({8{1'b0}}), .out(F), .sel(ALUop));
  nor nor_2 (ZF, F[0], F[1], F[2], F[3], F[4], F[5], F[6], F[7]);
endmodule

module control (
  input  [3:0] OpCode,
  output [2:0] ALUOp,
  output REG_WRT
);

  ROM #(.addrWidth(4), .dataWidth(4)) rom_1 (.addr(OpCode), .data({REG_WRT, ALUOp}));  // open: sel

  // Notes on the sheet:
  //   contents of rom_1 (hex, n*v repeats v):
  //   0 1 d e 4 5 6 7 b 9 1 a e 8 8 9
endmodule

module Ins_memory (
  input  [3:0] PC,
  output [19:0] Instruction_0_19
);

  instruction_memory instruction_memory_1 (.PC(PC), .Instruction_0_19(Instruction_0_19));

  // Notes on the sheet:
  //   Instruction Memory
endmodule

module Data_memory (
  input  [7:0] Address,
  input  [7:0] Data_Input,
  input  Store,
  input  Chip_Select,
  input  Clock,
  input  Load,
  input  Clear,
  output [7:0] Data_Loaded
);

  RAM #(.bus("separate")) ram_1 (
    .addr(Address), .din(Data_Input), .data(Data_Loaded), .str(Store), .sel(Chip_Select), .clk(Clock),
    .ld(Load), .clr(Clear));

  // Notes on the sheet:
  //   Data Memory
endmodule

module EX_MEM_REG (
  input  [7:0] alu_result,
  input  [3:0] reg_rd_addrs,
  input  in_3,
  input  clear,
  input  clk,
  output [7:0] alu_reslt,
  output [3:0] reg_rd_addrs_2,
  output reg_wrt
);

  Register u_alu_result (.D(alu_result), .en(1'b1), .Q(alu_reslt), .clk(clk), .clr(clear));
  Register #(.width(4)) reg_rd (.D(reg_rd_addrs), .en(1'b1), .Q(reg_rd_addrs_2), .clk(clk), .clr(clear));
  Register #(.width(1)) WB (.D(in_3), .en(1'b1), .Q(reg_wrt), .clk(clk), .clr(clear));
endmodule

module MEM_WB_REG (
  input  [7:0] alu_result,
  input  [3:0] reg_rd_addrs,
  input  in_3,
  input  clear,
  input  clk,
  output [7:0] alu_reslt,
  output [3:0] reg_rd_addrs_2,
  output reg_wrt
);

  Register u_alu_result (.D(alu_result), .en(1'b1), .Q(alu_reslt), .clk(clk), .clr(clear));
  Register #(.width(4)) reg_rd (.D(reg_rd_addrs), .en(1'b1), .Q(reg_rd_addrs_2), .clk(clk), .clr(clear));
  Register #(.width(1)) register_1 (.D(in_3), .en(1'b1), .Q(reg_wrt), .clk(clk), .clr(clear));
endmodule

module ID_EX_REG (
  input  [7:0] reg_rs_data,
  input  [7:0] reg_rt_data,
  input  [3:0] reg_rd_address,
  input  [3:0] reg_rs_address,
  input  [3:0] reg_rt_address,
  input  [2:0] ALUOP,
  input  REG_WRT,
  input  clear,
  input  clk,
  output [7:0] reg_rs_data_2,
  output [7:0] reg_rt_data_2,
  output [3:0] reg_rd_address_2,
  output [3:0] reg_rs_address_2,
  output [3:0] reg_rt_address_2,
  output [2:0] ALUOP_2,
  output reg_wrt_2
);

  Register read_reg1_data (.D(reg_rs_data), .en(1'b1), .Q(reg_rs_data_2), .clk(clk), .clr(clear));
  Register read_reg2_data (.D(reg_rt_data), .en(1'b1), .Q(reg_rt_data_2), .clk(clk), .clr(clear));
  Register #(.width(4)) reg_rd (.D(reg_rd_address), .en(1'b1), .Q(reg_rd_address_2), .clk(clk), .clr(clear));
  Register #(.width(4)) reg_rs (.D(reg_rs_address), .en(1'b1), .Q(reg_rs_address_2), .clk(clk), .clr(clear));
  Register #(.width(4)) reg_rt (.D(reg_rt_address), .en(1'b1), .Q(reg_rt_address_2), .clk(clk), .clr(clear));
  Register #(.width(3)) EX (.D(ALUOP), .en(1'b1), .Q(ALUOP_2), .clk(clk), .clr(clear));
  Register #(.width(1)) WB (.D(REG_WRT), .en(1'b1), .Q(reg_wrt_2), .clk(clk), .clr(clear));
endmodule

module Forwarding_Unit (
  input  [3:0] ID_EX_Reg_rt,
  input  [3:0] ID_EX_Reg_rs,
  input  [3:0] MEM_WB_Red_rd,
  input  [3:0] EX_MEM_Reg_rd,
  output [1:0] FORWARD_A,
  output [1:0] FORWARD_B
);

  wire nor_1_out, nor_2_out, nor_3_out, nor_4_out, or_1_out, or_2_out;
  wire [3:0] and_4_out, subtractor_1_out, subtractor_2_out, subtractor_3_out, subtractor_4_out;

  Subtractor #(.width(4)) subtractor_1 (
    .a(EX_MEM_Reg_rd), .b(ID_EX_Reg_rs), .out(subtractor_1_out));  // open: bin, bout
  Subtractor #(.width(4)) subtractor_2 (
    .a(EX_MEM_Reg_rd), .b(ID_EX_Reg_rt), .out(subtractor_2_out));  // open: bin, bout
  Subtractor #(.width(4)) subtractor_3 (
    .a(MEM_WB_Red_rd), .b(ID_EX_Reg_rs), .out(subtractor_3_out));  // open: bin, bout
  Subtractor #(.width(4)) subtractor_4 (
    .a(MEM_WB_Red_rd), .b(ID_EX_Reg_rt), .out(subtractor_4_out));  // open: bin, bout
  or or_1 (or_1_out, EX_MEM_Reg_rd[0], EX_MEM_Reg_rd[1], EX_MEM_Reg_rd[2], EX_MEM_Reg_rd[3]);
  nor nor_1 (nor_1_out, subtractor_2_out[0], subtractor_2_out[1], subtractor_2_out[2], subtractor_2_out[3]);
  nor nor_2 (nor_2_out, subtractor_1_out[0], subtractor_1_out[1], subtractor_1_out[2], subtractor_1_out[3]);
  nor nor_3 (nor_3_out, subtractor_3_out[0], subtractor_3_out[1], subtractor_3_out[2], subtractor_3_out[3]);
  nor nor_4 (nor_4_out, subtractor_4_out[0], subtractor_4_out[1], subtractor_4_out[2], subtractor_4_out[3]);
  and and_1 (and_4_out[3], or_1_out, nor_2_out);
  and and_2 (and_4_out[2], or_1_out, nor_1_out);
  or or_2 (or_2_out, MEM_WB_Red_rd[0], MEM_WB_Red_rd[1], MEM_WB_Red_rd[2], MEM_WB_Red_rd[3]);
  and and_3 (and_4_out[1], nor_3_out, or_2_out);
  and and_4 (and_4_out[0], nor_4_out, or_2_out);
  ROM #(.addrWidth(4), .dataWidth(4)) rom_1 (.addr(and_4_out), .data({FORWARD_A, FORWARD_B}), .sel(1'b1));

  // Notes on the sheet:
  //   contents of rom_1 (hex, n*v repeats v):
  //   0 1 4 5 2 2 6 6 8 9 8 9 4*a
endmodule

module IF_ID_REG (
  input  [19:0] Instruction,
  input  clk,
  input  clr,
  output [19:0] Instruction_2
);

  Register #(.width(20)) IF_ID_REG (.D(Instruction), .en(1'b1), .Q(Instruction_2), .clk(clk), .clr(clr));
endmodule
