// Logisim project 2 bit alu.circ as structural Verilog: 2 circuits, main circuit main
module main (
  input  s2,
  input  s1,
  input  s0,
  input  A,
  input  B,
  output out_6,
  output out_7
);

  wire and_1_out, and_2_out, and_3_out, and_4_out, not_1_out, not_2_out, not_3_out, not_4_out, or_1_out,
       or_2_out;

  not not_1 (not_1_out, s0);
  not not_2 (not_2_out, s1);
  and and_1 (and_1_out, s1, s0);
  not not_3 (not_3_out, s1);
  not not_4 (not_4_out, s0);
  and and_2 (and_2_out, s2, not_1_out);
  and and_3 (and_3_out, B, not_2_out, s0);
  and and_4 (and_4_out, B, not_3_out, not_4_out);
  or or_1 (or_1_out, A, and_3_out);
  or or_2 (or_2_out, and_1_out, and_4_out);
  Adder #(.width(1)) adder_1 (.a(or_1_out), .b(or_2_out), .out(out_6), .cin(and_2_out), .cout(out_7));
endmodule

module _2_bit_ckt (
  input  S2,
  input  S1,
  input  S0,
  input  A0,
  input  B0,
  input  A1,
  input  B1,
  output out_8,
  output out_9,
  output out_10
);

  wire and_1_out, main_1_out_7, not_1_out;

  not not_1 (not_1_out, S0);
  main main_1 (.s2(S2), .s1(S1), .s0(S0), .A(A0), .B(B0), .out_6(out_8), .out_7(main_1_out_7));
  and and_1 (and_1_out, not_1_out, main_1_out_7);
  main main_2 (.s2(and_1_out), .s1(S1), .s0(S0), .A(A1), .B(B1), .out_6(out_9), .out_7(out_10));
endmodule
