// Logisim project 4-Bit-ALU Final.circ as structural Verilog: 3 circuits, main circuit 1 bit combinational ckt
module _1_bit_combinational_ckt (
  input  s2,
  input  s1,
  input  s0,
  input  A,
  input  B,
  output F,
  output out_7
);

  wire and_1_out, and_2_out, and_3_out, and_4_out, not_1_out, not_2_out, or_1_out, or_2_out;

  not not_1 (not_1_out, s0);
  not not_2 (not_2_out, s1);
  and and_1 (and_1_out, s1, s0);
  and and_2 (and_2_out, s2, not_1_out);
  and and_3 (and_3_out, B, not_2_out, s0);
  and and_4 (and_4_out, B, not_2_out, not_1_out);
  or or_1 (or_1_out, A, and_3_out);
  or or_2 (or_2_out, and_1_out, and_4_out);
  Adder #(.width(1)) adder_1 (.a(or_1_out), .b(or_2_out), .out(F), .cin(and_2_out), .cout(out_7));
endmodule

module _4_bit_ckt (
  input  [3:0] B,
  input  [3:0] A,
  input  [2:0] Select,
  output [3:0] F,
  output Z,
  output S,
  output V,
  output C
);

  wire _1_bit_combinational_ckt_with_adder_p6, n1_bit_combinational_ckt_1_p6, n1_bit_combinational_ckt_2_p6,
       n1_bit_combinational_ckt_3_p6, not_1_out;

  not not_1 (not_1_out, Select[0]);
  // _1_bit_combinational_ckt _1_bit_combinational_ckt_with_adder: pin names not known; wires that end beside it: Select[2], Select[1], Select[0], A[0], B[0], _1_bit_combinational_ckt_with_adder_p6, F[0]
  // _1_bit_combinational_ckt 1_bit_combinational_ckt_1: pin names not known; wires that end beside it: _1_bit_combinational_ckt_with_adder_p6, Select[1], Select[0], A[1], B[1], n1_bit_combinational_ckt_1_p6, F[1]
  // _1_bit_combinational_ckt 1_bit_combinational_ckt_2: pin names not known; wires that end beside it: n1_bit_combinational_ckt_1_p6, Select[1], Select[0], A[2], B[2], n1_bit_combinational_ckt_2_p6, F[2]
  // _1_bit_combinational_ckt 1_bit_combinational_ckt_3: pin names not known; wires that end beside it: n1_bit_combinational_ckt_2_p6, Select[1], Select[0], A[3], B[3], n1_bit_combinational_ckt_3_p6, F[3]
  and and_1 (C, n1_bit_combinational_ckt_3_p6, not_1_out);
  nor nor_1 (Z, F[3], F[2], F[1], F[0]);
  xor xor_1 (V, n1_bit_combinational_ckt_2_p6, C);

  assign S = F[3];
endmodule

module Final_alu (
  input  [3:0] A,
  input  [3:0] B,
  input  [2:0] Select,
  output C,
  output V,
  output S,
  output Z,
  output [3:0] Output
);

  _4_bit_ckt _4__BIT_ALU (.A(A), .B(B), .F(Output), .V(V), .S(S), .C(C), .Z(Z), .Select(Select));
endmodule
