// Logisim project test_log.circ as structural Verilog: 2 circuits, main circuit main
module main (
  input  A,
  input  B,
  input  C,
  output out_4
);

  wire or_1_out;

  or or_1 (or_1_out, B, C);
  and and_1 (out_4, ~A, or_1_out);  // AND_Gate
endmodule

module ckt1 (
  input  A,
  input  B,
  input  C,
  output out_4
);

  wire or_1_out;

  or or_1 (or_1_out, B, C);
  and and_1 (out_4, ~A, or_1_out);  // AND_Gate
endmodule
